# Fritzing sketch garage (saved by Fritzing 0.9.3b)
circuit board: 8.46667cm x 5.64444cm
breadboards: 2

parts:
  Part1 = Arduino Nano (Rev3.0)
  hc-sr1 = hc-sr04
  LED1 = LED - 3mm [color="Red (633nm)" package="3 mm [THT]"]
  LED3 = LED - 3mm [color="Green (565nm)" package="3 mm [THT]"]
  R2 = Resistor [tolerance=±5% resistance=220 package="1206 [SMD]"]
  LED2 = LED - 3mm [color="Yellow (595nm)" package="3 mm [THT]"]
  R3 = Resistor [tolerance=±5% resistance=220 package="1206 [SMD]"]
  R4 = Resistor [tolerance=±5% resistance=220 package="1206 [SMD]"]
  MCU1 = Raspberry Pi Zero
  R5 = Resistor [tolerance=±5% resistance=1.5k package=THT]
  Q1 = NPN-Transistor [package="TO92 [THT]"]
  hc-sr2 = hc-sr04
  R6 = Resistor [tolerance=±5% resistance=330 package="2512 [SMD]"]
  R7 = Resistor [tolerance=±5% resistance=470 package="2512 [SMD]"]
  U1 = Sharp PC817 [package=THT]

nets:
  GND: Part1.RESET, Part1.GND, hc-sr1.GND, LED1.cathode, LED3.cathode, LED2.cathode, Q1.C
  N1: Part1.D2, hc-sr1.Echo
  N2: Part1.D3, hc-sr1.Trig
  N3: Part1.D4, R4.Pin_1
  N4: Part1.D5, R3.Pin_1
  N5: Part1.D6, Part1.D7, R2.Pin_1
  VCC: Part1.VIN, hc-sr1.VCC, MCU1.pin_2, MCU1.pin_4, hc-sr2.VCC
  N6: LED1.anode, R2.Pin_0
  N7: LED3.anode, R4.Pin_0
  N8: LED2.anode, R3.Pin_0
  N9: MCU1.pin_3, R5.Pin_1
  N10: MCU1.pin_6, MCU1.pin_34, MCU1.pin_39, Q1.E, hc-sr2.GND, R7.Pin_1, U1.Pin_2
  N11: MCU1.pin_8, U1.Pin_1
  N12: MCU1.pin_10, R7.Pin_0
  N13: MCU1.pin_12, hc-sr2.Trig
  N14: R5.Pin_0, Q1.B
  N15: hc-sr2.Echo, R6.Pin_1

notes:
  Abstandswarner
  Garagentorkontrolle

// code stored in the sketch: Untitled.ino

